# Fritzing sketch wiring-diagram (saved by Fritzing 0.9.3b)
breadboards: 1

parts:
  S1 = Momentary Switch [package=tactile-pth]
  Grove1 = Grove OLED 128x96
  Raspberry_Pi1 = Raspberry Pi B+

nets:
  N1: S1.3, Raspberry_Pi1.GPIO16
  GND: S1.4, Grove1.GND, Raspberry_Pi1.GND
